# Fritzing sketch monolith (saved by Fritzing 0.9.3b)
breadboards: 1

parts:
  Teensy_3_2 = Teensy 3.0  # not connected
  S3 = Pushbutton [package="[THT]"]

nets:
  N1: S3.Pin_1, S3.Pin_2
  N2: S3.Pin_3, S3.Pin_4

notes:
  5V Outputs to Analog CV sync
  Capacitive sensor inputs
  Sensor input | Digital output
  A1 | 2
  A2 | 3
  A3 | 4
  A4 | 5
  A5 | 6
  A8 | 7
  A9 | 8
  25 | 9
  Reset Max Capacitance reading
  BPM Down Sensor
  BPM Up Sensor
  CV sync input
